// Logisim project Guia_0503.circ as structural Verilog: 1 circuit, main circuit main
module main (
  input  a,
  input  b,
  output out_3
);

  wire nor_1_out, not_1_out;

  not not_1 (not_1_out, a);
  nor nor_1 (nor_1_out, not_1_out, b);
  not not_2 (out_3, nor_1_out);

  // Notes on the sheet:
  //   ~a | b = ~(~(~a|b)
endmodule
