// Logisim project Guia_0505.circ as structural Verilog: 1 circuit, main circuit main
module main (
  input  a,
  input  b,
  input  in_3,
  input  in_4,
  output out_5,
  output out_6
);

  wire and_1_out, and_2_out, nor_1_out, not_1_out, not_2_out;

  not not_1 (not_1_out, b);
  not not_2 (not_2_out, a);
  and and_1 (and_1_out, a, b);
  and and_2 (and_2_out, not_2_out, not_1_out);
  xnor xnor_1 (out_6, in_3, in_4);
  nor nor_1 (nor_1_out, and_1_out, and_2_out);
  not not_3 (out_5, nor_1_out);

  // Notes on the sheet:
  //   $
  //   ~(a^b) =    a*b + (~a)*(~b) =     ~(~(a*b + (~a)*(~b)))
  //   Circuito em funcao de XNor
  //   Circuito em função de Nor
endmodule
