// Logisim project Guia_0506.circ as structural Verilog: 1 circuit, main circuit main
module main (
  input  a,
  input  b,
  input  in_3,
  input  in_4,
  output out_5,
  output out_6
);

  wire not_1_out, not_2_out, or_1_out, or_2_out;

  not not_1 (not_1_out, b);
  not not_2 (not_2_out, a);
  or or_1 (or_1_out, a, not_1_out);
  or or_2 (or_2_out, not_2_out, b);
  xor xor_1 (out_6, in_3, in_4);
  nand nand_1 (out_5, or_1_out, or_2_out);

  // Notes on the sheet:
  //   a ^ b = ~a*b + a*(~b) =  ~(~(~a*b + a*(~b))) = ~(a+(~b)  * ~a+b)  
  //   Circuito em função de Xor
  //   Circuito em função de Nand
endmodule
