// Logisim project Guia_06_01_A.circ as structural Verilog: 1 circuit, main circuit main
module main (
  input  x,
  input  y,
  input  z,
  output out_4
);

  wire and_1_out, and_2_out, not_1_out;

  not not_1 (not_1_out, y);
  and and_1 (and_1_out, x, z);
  and and_2 (and_2_out, not_1_out, z);
  or or_1 (out_4, and_1_out, and_2_out);
endmodule
