// Logisim project Guia13_02.circ as structural Verilog: 1 circuit, main circuit main
module main (
  input  load,
  input  clr,
  output out_3,
  output out_4,
  output out_5,
  output out_6
);

  wire clock_1_out, j_k_ff_2_q, j_k_ff_3_q, j_k_ff_4_q;

  Clock clock_1 (.out(clock_1_out));
  J_K_Flip_Flop #(.Pre_Clr_Positions("LEGACY"), .enable("true"), .NewFFLayout("false")) j_k_ff_1 (
    .J(load), .clk(j_k_ff_2_q), .K(load), .Qn(out_3), .reset(clr));  // open: Q, preset, en
  J_K_Flip_Flop #(.Pre_Clr_Positions("LEGACY"), .enable("true"), .NewFFLayout("false")) j_k_ff_2 (
    .J(load), .clk(j_k_ff_3_q), .K(load), .Q(j_k_ff_2_q), .Qn(out_4), .reset(clr));  // open: preset, en
  J_K_Flip_Flop #(.Pre_Clr_Positions("LEGACY"), .enable("true"), .NewFFLayout("false")) j_k_ff_3 (
    .J(load), .clk(j_k_ff_4_q), .K(load), .Q(j_k_ff_3_q), .Qn(out_5), .reset(clr));  // open: preset, en
  J_K_Flip_Flop #(.Pre_Clr_Positions("LEGACY"), .enable("true"), .NewFFLayout("false")) j_k_ff_4 (
    .J(load), .clk(clock_1_out), .K(load), .Q(j_k_ff_4_q), .Qn(out_6), .reset(clr));  // open: preset, en
endmodule
