// Logisim project Guia13_04.circ as structural Verilog: 1 circuit, main circuit main
module main (
  input  load,
  input  clr,
  output a,
  output b,
  output c,
  output d
);

  wire clock_1_out, j_k_ff_1_qn, j_k_ff_2_qn, j_k_ff_3_qn, nand_1_out, nand_2_out, not_1_out, not_2_out;

  Clock clock_1 (.out(clock_1_out));
  nand nand_1 (nand_1_out, clr, nand_2_out);
  not not_1 (not_1_out, d);
  nand nand_2 (nand_2_out, not_1_out, c, not_2_out, a);
  not not_2 (not_2_out, b);
  J_K_Flip_Flop #(.Pre_Clr_Positions("LEGACY"), .enable("true"), .NewFFLayout("false")) j_k_ff_1 (
    .J(load), .clk(clock_1_out), .K(load), .Q(d), .Qn(j_k_ff_1_qn), .reset(nand_1_out));  // open: preset, en
  J_K_Flip_Flop #(.Pre_Clr_Positions("LEGACY"), .enable("true"), .NewFFLayout("false")) j_k_ff_2 (
    .J(load), .clk(j_k_ff_1_qn), .K(load), .Q(c), .Qn(j_k_ff_2_qn), .reset(nand_1_out));  // open: preset, en
  J_K_Flip_Flop #(.Pre_Clr_Positions("LEGACY"), .enable("true"), .NewFFLayout("false")) j_k_ff_3 (
    .J(load), .clk(j_k_ff_2_qn), .K(load), .Q(b), .Qn(j_k_ff_3_qn), .reset(nand_1_out));  // open: preset, en
  J_K_Flip_Flop #(.Pre_Clr_Positions("LEGACY"), .enable("true"), .NewFFLayout("false")) j_k_ff_4 (
    .J(load), .clk(j_k_ff_3_qn), .K(load), .Q(a), .reset(nand_1_out));  // open: Qn, preset, en
endmodule
