// Logisim project Guia17_03.circ as structural Verilog: 1 circuit, main circuit main
module main (
  input  c,
  input  clk
);

  wire and_1_out, and_2_out, and_3_out, and_4_out, j_k_ff_1_q, j_k_ff_2_q, not_1_out, not_2_out, or_1_out,
       or_2_out;

  and and_1 (and_1_out, ~j_k_ff_1_q, j_k_ff_2_q, c);  // AND_Gate
  and and_2 (and_2_out, j_k_ff_1_q, ~j_k_ff_2_q, c);  // AND_Gate
  and and_3 (and_3_out, ~j_k_ff_1_q, ~j_k_ff_2_q, c);  // AND_Gate
  and and_4 (and_4_out, j_k_ff_1_q, j_k_ff_2_q, c);
  or or_1 (or_1_out, and_1_out, and_2_out);
  or or_2 (or_2_out, and_3_out, and_4_out);
  J_K_Flip_Flop j_k_ff_1 (.J(or_1_out), .clk(clk), .K(not_1_out), .Q(j_k_ff_1_q));  // open: Qn, preset, reset
  not not_1 (not_1_out, or_1_out);
  J_K_Flip_Flop j_k_ff_2 (.J(or_2_out), .clk(clk), .K(not_2_out), .Q(j_k_ff_2_q));  // open: Qn, preset, reset
  not not_2 (not_2_out, or_2_out);

  // Notes on the sheet:
  //   s1 = a
  //   s2 = b
endmodule
