// Logisim project Guia17_05.circ as structural Verilog: 1 circuit, main circuit main
module main (
  input  load,
  input  clk,
  output out_3,
  output out_4,
  output out_5
);

  wire t_ff_1_qn, t_ff_2_qn;

  T_Flip_Flop #(.Pre_Clr_Positions("LEGACY"), .enable("true"), .NewFFLayout("false")) t_ff_1 (
    .clk(clk), .T(load), .Q(out_5), .Qn(t_ff_1_qn));  // open: preset, reset, en
  T_Flip_Flop #(.Pre_Clr_Positions("LEGACY"), .enable("true"), .NewFFLayout("false")) t_ff_2 (
    .clk(t_ff_1_qn), .T(load), .Q(out_4), .Qn(t_ff_2_qn));  // open: preset, reset, en
  T_Flip_Flop #(.Pre_Clr_Positions("LEGACY"), .enable("true"), .NewFFLayout("false")) t_ff_3 (
    .clk(t_ff_2_qn), .T(load), .Q(out_3));  // open: Qn, preset, reset, en
endmodule
