// Logisim project Recup01.circ as structural Verilog: 1 circuit, main circuit main
module main (
  input  a,
  input  b,
  input  c,
  input  d,
  input  a_2,
  input  b_2,
  input  c_2,
  input  d_2,
  input  a_3,
  input  b_3,
  input  c_3,
  input  d_3,
  input  a_4,
  input  b_4,
  input  c_4,
  input  d_4,
  input  a_5,
  input  b_5,
  input  c_5,
  input  d_5,
  input  a_6,
  input  b_6,
  input  c_6,
  input  d_6,
  input  a_7,
  input  b_7,
  input  c_7,
  input  d_7,
  input  a_8,
  input  b_8,
  input  c_8,
  input  d_8,
  output out_33,
  output out_34,
  output out_35,
  output out_36,
  output out_37,
  output out_38,
  output out_39,
  output out_40
);

  wire and_1_out, and_2_out, and_3_out, and_4_out, and_5_out, and_6_out, and_7_out, and_8_out, and_10_out,
       and_11_out, and_12_out, nand_1_out, nand_2_out, nand_3_out, nand_4_out, nand_5_out, nand_6_out,
       nand_7_out, nand_8_out, nand_9_out, nand_10_out, nand_11_out, nand_12_out, nand_13_out, nand_14_out,
       nand_15_out, nand_17_out, nand_18_out, nand_19_out, nand_20_out, nand_21_out, nand_22_out,
       nand_23_out, nand_24_out, nand_25_out, nor_1_out, nor_2_out, nor_3_out, nor_4_out, nor_5_out,
       nor_6_out, nor_7_out, nor_8_out, nor_9_out, nor_10_out, nor_11_out, nor_12_out, nor_13_out,
       nor_14_out, nor_15_out, nor_16_out, nor_17_out, nor_18_out, nor_19_out, nor_21_out, nor_22_out,
       nor_23_out, nor_24_out, nor_25_out, nor_26_out, nor_27_out, nor_28_out, nor_29_out, nor_30_out,
       nor_31_out, not_1_out, not_2_out, not_3_out, not_4_out, not_5_out, not_6_out, not_7_out, not_8_out,
       not_9_out, not_10_out, not_11_out, not_12_out, not_13_out, not_14_out, not_15_out, not_16_out,
       or_1_out, or_2_out, or_3_out, or_4_out, or_5_out, or_6_out, or_7_out, or_8_out, or_9_out, or_12_out,
       or_13_out, or_14_out, or_15_out;

  not not_1 (not_1_out, b);
  not not_2 (not_2_out, a);
  not not_3 (not_3_out, a_5);
  not not_4 (not_4_out, b_5);
  not not_5 (not_5_out, c);
  not not_6 (not_6_out, d);
  not not_7 (not_7_out, d_5);
  not not_8 (not_8_out, c_5);
  and and_1 (and_1_out, not_2_out, not_1_out, not_5_out, not_6_out);
  and and_2 (and_2_out, not_2_out, not_1_out, not_5_out, d);
  and and_3 (and_3_out, not_2_out, not_1_out, c, not_6_out);
  and and_4 (and_4_out, not_2_out, not_1_out, c, d);
  and and_5 (and_5_out, not_2_out, b, not_5_out, d);
  and and_6 (and_6_out, a, not_1_out, not_5_out, not_6_out);
  and and_7 (and_7_out, a, not_1_out, not_5_out, not_6_out);
  and and_8 (and_8_out, a, b, not_5_out, d);
  or or_1 (or_1_out, a_5, not_4_out, c_5, d_5);
  or or_2 (or_2_out, a_5, not_4_out, not_8_out, d_5);
  or or_3 (or_3_out, a_5, not_4_out, not_8_out, not_7_out);
  or or_4 (or_4_out, not_3_out, b_5, c_5, not_7_out);
  or or_5 (or_5_out, not_3_out, b_5, not_8_out, d_5);
  or or_6 (or_6_out, not_3_out, b_5, not_8_out, not_7_out);
  or or_7 (or_7_out, not_3_out, not_4_out, c_5, d_5);
  or or_8 (or_8_out, not_3_out, not_4_out, not_8_out, d_5);
  or or_9 (or_9_out, not_3_out, not_4_out, not_8_out, not_7_out);
  or or_10 (out_36, and_1_out, and_2_out, and_3_out, and_4_out, and_5_out, and_6_out, and_7_out, and_8_out);
  and and_9 (out_40, or_1_out, or_2_out, or_3_out, or_4_out, or_5_out, or_6_out, or_7_out, or_8_out, or_9_out);
  not not_9 (not_9_out, a_2);
  not not_10 (not_10_out, d_2);
  not not_11 (not_11_out, b_2);
  not not_12 (not_12_out, c_2);
  not not_13 (not_13_out, b_6);
  not not_14 (not_14_out, a_6);
  and and_10 (and_10_out, not_9_out, not_11_out);
  and and_11 (and_11_out, b_2, not_12_out, d_2);
  and and_12 (and_12_out, not_11_out, not_12_out, not_10_out);
  not not_15 (not_15_out, d_6);
  not not_16 (not_16_out, c_6);
  or or_11 (out_33, and_10_out, and_11_out, and_12_out);
  or or_12 (or_12_out, not_13_out, not_16_out);
  or or_13 (or_13_out, not_14_out, not_16_out);
  or or_14 (or_14_out, not_13_out, d_6);
  or or_15 (or_15_out, not_14_out, b_6, not_15_out);
  and and_13 (out_37, or_12_out, or_13_out, or_14_out, or_15_out);
  nand nand_1 (nand_1_out, a_3, a_3);
  nand nand_2 (nand_2_out, b_3, b_3);
  nand nand_3 (nand_3_out, c_3, c_3);
  nand nand_4 (nand_4_out, b_3, b_3);
  nand nand_5 (nand_5_out, c_3, c_3);
  nand nand_6 (nand_6_out, d_3, d_3);
  nand nand_7 (nand_7_out, nand_1_out, nand_2_out);
  nand nand_8 (nand_8_out, b_3, nand_3_out, d_3);
  nand nand_9 (nand_9_out, nand_4_out, nand_5_out, nand_6_out);
  nand nand_10 (nand_10_out, nand_7_out, nand_7_out);
  nand nand_11 (nand_11_out, nand_8_out, nand_8_out);
  nand nand_12 (nand_12_out, nand_9_out, nand_9_out);
  nor nor_1 (nor_1_out, b_7, b_7);
  nor nor_2 (nor_2_out, c_7, c_7);
  nor nor_3 (nor_3_out, a_7, a_7);
  nor nor_4 (nor_4_out, c_7, c_7);
  nor nor_5 (nor_5_out, b_7, b_7);
  nor nor_6 (nor_6_out, a_7, a_7);
  nor nor_7 (nor_7_out, d_7, d_7);
  nor nor_8 (nor_8_out, nor_1_out, nor_2_out);
  nor nor_9 (nor_9_out, nor_3_out, nor_4_out);
  nor nor_10 (nor_10_out, nor_5_out, d_7);
  nand nand_13 (nand_13_out, nand_10_out, nand_10_out);
  nand nand_14 (nand_14_out, nand_11_out, nand_11_out);
  nand nand_15 (nand_15_out, nand_12_out, nand_12_out);
  nor nor_11 (nor_11_out, nor_8_out, nor_8_out);
  nor nor_12 (nor_12_out, nor_9_out, nor_9_out);
  nor nor_13 (nor_13_out, nor_10_out, nor_10_out);
  nor nor_14 (nor_14_out, nor_6_out, b_7, nor_7_out);
  nand nand_16 (out_34, nand_13_out, nand_14_out, nand_15_out);
  nor nor_15 (nor_15_out, nor_12_out, nor_12_out);
  nor nor_16 (nor_16_out, nor_13_out, nor_13_out);
  nor nor_17 (nor_17_out, nor_14_out, nor_14_out);
  nor nor_18 (nor_18_out, nor_11_out, nor_11_out);
  nor nor_19 (nor_19_out, nor_17_out, nor_17_out);
  nor nor_20 (out_38, nor_18_out, nor_15_out, nor_16_out, nor_19_out);
  nand nand_17 (nand_17_out, a_4, a_4);
  nand nand_18 (nand_18_out, b_4, b_4);
  nand nand_19 (nand_19_out, c_4, c_4);
  nand nand_20 (nand_20_out, b_4, b_4);
  nand nand_21 (nand_21_out, c_4, c_4);
  nand nand_22 (nand_22_out, d_4, d_4);
  nand nand_23 (nand_23_out, nand_17_out, nand_18_out);
  nand nand_24 (nand_24_out, b_4, nand_19_out, d_4);
  nand nand_25 (nand_25_out, nand_20_out, nand_21_out, nand_22_out);
  nand nand_26 (out_35, nand_23_out, nand_24_out, nand_25_out);
  nor nor_21 (nor_21_out, b_8, b_8);
  nor nor_22 (nor_22_out, c_8, c_8);
  nor nor_23 (nor_23_out, a_8, a_8);
  nor nor_24 (nor_24_out, c_8, c_8);
  nor nor_25 (nor_25_out, b_8, b_8);
  nor nor_26 (nor_26_out, a_8, a_8);
  nor nor_27 (nor_27_out, d_8, d_8);
  nor nor_28 (nor_28_out, nor_21_out, nor_22_out);
  nor nor_29 (nor_29_out, nor_23_out, nor_24_out);
  nor nor_30 (nor_30_out, nor_25_out, d_8);
  nor nor_31 (nor_31_out, nor_26_out, b_8, nor_27_out);
  nor nor_32 (out_39, nor_28_out, nor_29_out, nor_30_out, nor_31_out);

  // Notes on the sheet:
  //   expressao canonica
  //   expressao canonica
  //   expressao simplificada
  //   expressao simplificada
  //   SOP
  //   PoS
  //   expressao com portas NAND
  //   expressao com portas NOR
  //   expressao comportas NAND simplificada 
  //   expressao com portas NOR simplificada
endmodule
