// Logisim project Recup02.circ as structural Verilog: 1 circuit, main circuit main
module main (
  input  x,
  input  y,
  output s
);

  wire and_1_out, not_1_out, not_2_out, or_1_out;

  not not_1 (not_1_out, y);
  and and_1 (and_1_out, not_1_out, x);
  or or_1 (or_1_out, y, x);
  not not_2 (not_2_out, and_1_out);
  or or_2 (s, not_2_out, or_1_out);

  // Notes on the sheet:
  //   NOT_1
  //   w1
  //   w2
  //   AND_1
  //   OR_1
  //   NOT_2
  //   w4
  //   w3
  //   OR_2
endmodule
