// Logisim project Recup03.circ as structural Verilog: 1 circuit, main circuit main
module main (
  input  a,
  input  b,
  input  c,
  input  d,
  input  a_2,
  input  b_2,
  input  c_2,
  output out_8,
  output out_9
);

  wire multiplexer_1_out, multiplexer_2_out, nand_1_out, nand_2_out, not_1_out, not_2_out, not_3_out;

  not not_1 (not_1_out, a_2);
  not not_2 (not_2_out, c_2);
  not not_3 (not_3_out, b_2);
  nand nand_1 (nand_1_out, a, c);
  nand nand_2 (nand_2_out, b, d);
  Multiplexer #(.enable("false")) multiplexer_1 (.in0(b_2), .in1(c_2), .out(multiplexer_1_out), .sel(a_2));
  Multiplexer #(.enable("false")) multiplexer_2 (.in0(not_1_out), .in1(not_3_out), .out(multiplexer_2_out), .sel(c_2));
  nand nand_3 (out_8, nand_1_out, nand_2_out);
  Multiplexer #(.enable("false")) multiplexer_3 (
    .in0(multiplexer_1_out), .in1(multiplexer_2_out), .out(out_9), .sel(not_2_out));
endmodule
