// Logisim project Recup05.circ as structural Verilog: 1 circuit, main circuit main
module main (
  input  [7:0] a,
  input  [7:0] b,
  input  [7:0] a_2,
  input  [7:0] b_2,
  output [7:0] out_5,
  output [7:0] out_6,
  output [7:0] out_7
);

  wire [7:0] not_1_out, not_2_out, not_3_out, not_4_out, xor_3_out, xor_4_out;

  assign not_1_out = ~a;  // NOT_Gate not_1, 8 bits wide
  assign not_2_out = ~a_2;  // NOT_Gate not_2, 8 bits wide
  assign not_3_out = ~b;  // NOT_Gate not_3, 8 bits wide
  assign not_4_out = ~b_2;  // NOT_Gate not_4, 8 bits wide
  assign out_5 = a ^ b;  // XOR_Gate xor_1, 8 bits wide
  assign out_6 = not_1_out ^ not_3_out;  // XOR_Gate xor_2, 8 bits wide
  assign xor_3_out = a_2 ^ b_2;  // XOR_Gate xor_3, 8 bits wide
  assign xor_4_out = not_2_out ^ not_4_out;  // XOR_Gate xor_4, 8 bits wide
  assign out_7 = xor_3_out | xor_4_out;  // OR_Gate or_1, 8 bits wide

  // Notes on the sheet:
  //   a)
  //   b)
endmodule
