// Logisim project R_0204b.circ as structural Verilog: 1 circuit, main circuit main
module main (
  input  a,
  input  b,
  input  c,
  output J,
  output k
);

  wire not_1_out, not_2_out;

  not not_1 (not_1_out, a);
  not not_2 (not_2_out, b);
  and and_1 (J, not_1_out, b, c);
  and and_2 (k, a, not_2_out, c);
endmodule
