// Logisim project R_0204d.circ as structural Verilog: 1 circuit, main circuit main
module main (
  input  a,
  input  b,
  input  c,
  output S,
  output R
);

  wire not_1_out, not_2_out;

  not not_1 (not_1_out, a);
  not not_2 (not_2_out, b);
  and and_1 (S, not_1_out, not_2_out, c);
  and and_2 (R, a, b, c);
endmodule
