// Logisim project R_0205a.circ as structural Verilog: 1 circuit, main circuit main
module main (
  input  clk,
  input  in_2,
  input  clr,
  output a,
  output b,
  output c,
  output d
);

  D_Flip_Flop #(.Pre_Clr_Positions("LEGACY"), .NewFFLayout("false")) d_ff_1 (
    .clk(clk), .D(in_2), .Q(a), .reset(clr));  // open: Qn, preset
  D_Flip_Flop #(.Pre_Clr_Positions("LEGACY"), .NewFFLayout("false")) d_ff_2 (
    .clk(clk), .D(a), .Q(b), .reset(clr));  // open: Qn, preset
  D_Flip_Flop #(.Pre_Clr_Positions("LEGACY"), .NewFFLayout("false")) d_ff_3 (
    .clk(clk), .D(b), .Q(c), .reset(clr));  // open: Qn, preset
  D_Flip_Flop #(.Pre_Clr_Positions("LEGACY"), .NewFFLayout("false")) d_ff_4 (
    .clk(clk), .D(c), .Q(d), .reset(clr));  // open: Qn, preset
endmodule
