// Logisim project R_0205d.circ as structural Verilog: 1 circuit, main circuit main
module main (
  input  clk,
  input  d,
  input  in_3,
  input  clr,
  output a,
  output b,
  output c,
  output d_2
);

  wire nand_1_out;

  nand nand_1 (nand_1_out, d, in_3);
  D_Flip_Flop #(.Pre_Clr_Positions("LEGACY"), .NewFFLayout("false")) d_ff_1 (
    .clk(clk), .D(nand_1_out), .Q(a), .reset(clr));  // open: Qn, preset
  D_Flip_Flop #(.Pre_Clr_Positions("LEGACY"), .NewFFLayout("false")) d_ff_2 (
    .clk(clk), .D(a), .Q(b), .reset(clr));  // open: Qn, preset
  D_Flip_Flop #(.Pre_Clr_Positions("LEGACY"), .NewFFLayout("false")) d_ff_3 (
    .clk(clk), .D(b), .Q(c), .reset(clr));  // open: Qn, preset
  D_Flip_Flop #(.Pre_Clr_Positions("LEGACY"), .NewFFLayout("false")) d_ff_4 (
    .clk(clk), .D(c), .Q(d_2), .reset(clr));  // open: Qn, preset
endmodule
