// Logisim project R_0205e.circ as structural Verilog: 1 circuit, main circuit main
module main (
  input  clk,
  input  in_2,
  input  clr,
  output a,
  output b,
  output c,
  output d
);

  wire d_ff_1_qn, d_ff_2_qn, d_ff_3_qn;

  D_Flip_Flop #(.Pre_Clr_Positions("LEGACY"), .NewFFLayout("false")) d_ff_1 (
    .clk(clk), .D(in_2), .Q(a), .Qn(d_ff_1_qn), .reset(clr));  // open: preset
  D_Flip_Flop #(.Pre_Clr_Positions("LEGACY"), .NewFFLayout("false")) d_ff_2 (
    .clk(clk), .D(d_ff_1_qn), .Q(b), .Qn(d_ff_2_qn), .reset(clr));  // open: preset
  D_Flip_Flop #(.Pre_Clr_Positions("LEGACY"), .NewFFLayout("false")) d_ff_3 (
    .clk(clk), .D(d_ff_2_qn), .Q(c), .Qn(d_ff_3_qn), .reset(clr));  // open: preset
  D_Flip_Flop #(.Pre_Clr_Positions("LEGACY"), .NewFFLayout("false")) d_ff_4 (
    .clk(clk), .D(d_ff_3_qn), .Q(d), .reset(clr));  // open: Qn, preset
endmodule
