// Logisim project estudos.circ as structural Verilog: 1 circuit, main circuit main
module main (
  input  x,
  input  select,
  input  y,
  input  x_2,
  input  y_2,
  input  w,
  input  z,
  input  select0,
  input  select1,
  input  in_10,
  input  in_11,
  input  in_12,
  input  in_13,
  input  in_14,
  input  in_15,
  input  in_16,
  input  in_17,
  input  in_18,
  input  in_19,
  input  in_20,
  output out_21,
  output out_22,
  output out_23
);

  wire and_1_out, and_2_out, and_3_out, and_4_out, and_5_out, and_6_out, and_7_out, and_8_out, and_9_out,
       and_10_out, and_11_out, and_12_out, and_13_out, and_14_out, not_1_out, not_2_out, not_3_out,
       not_4_out, not_5_out, not_6_out, not_7_out, not_8_out, not_9_out, not_10_out, not_11_out, not_12_out,
       not_13_out, not_14_out, not_15_out, not_16_out, not_17_out;

  not not_1 (not_1_out, select);
  and and_1 (and_1_out, x, not_1_out);
  and and_2 (and_2_out, select, y);
  or or_1 (out_21, and_1_out, and_2_out);
  and and_3 (and_3_out, x_2, not_2_out, not_3_out);
  not not_2 (not_2_out, select0);
  not not_3 (not_3_out, select1);
  and and_4 (and_4_out, y_2, not_4_out, select1);
  not not_4 (not_4_out, select0);
  and and_5 (and_5_out, w, select0, not_5_out);
  not not_5 (not_5_out, select1);
  and and_6 (and_6_out, z, select1, select0);
  or or_2 (out_22, and_3_out, and_4_out, and_5_out, and_6_out);
  not not_6 (not_6_out, in_18);
  and and_7 (and_7_out, in_10, not_6_out, not_7_out, not_8_out);
  not not_7 (not_7_out, in_19);
  not not_8 (not_8_out, in_20);
  not not_9 (not_9_out, in_18);
  and and_8 (and_8_out, in_11, not_9_out, not_10_out, in_20);
  not not_10 (not_10_out, in_19);
  not not_11 (not_11_out, in_18);
  and and_9 (and_9_out, in_12, not_11_out, in_19, not_12_out);
  not not_12 (not_12_out, in_20);
  not not_13 (not_13_out, in_18);
  and and_10 (and_10_out, in_13, not_13_out, in_19, in_20);
  and and_11 (and_11_out, in_14, in_18, not_14_out, not_15_out);
  not not_14 (not_14_out, in_19);
  not not_15 (not_15_out, in_20);
  and and_12 (and_12_out, in_15, in_18, not_16_out, in_20);
  not not_16 (not_16_out, in_19);
  and and_13 (and_13_out, in_16, in_18, in_19, not_17_out);
  not not_17 (not_17_out, in_20);
  and and_14 (and_14_out, in_17, in_18, in_19, in_20);
  or or_3 (out_23, and_7_out, and_8_out, and_9_out, and_10_out, and_11_out, and_12_out, and_13_out, and_14_out);
endmodule
